# Fritzing sketch sketch (saved by Fritzing 0.9.2b)
breadboards: 1

parts:
  PIR1 = PIR sensor
  U1 = attiny85 [package=dip]
  LED1 = LED - 5mm [color="Red (633nm)" package="5 mm [THT]"]
  J1 = Piezo Speaker
  R1 = Resistor [tolerance=±5% resistance=220 package=THT]
  R2 = Resistor [tolerance=±5% resistance=220 package=THT]
  U2 = RELAY [package=relay-g5q]

nets:
  N1: PIR1.VDD, U1.Pin_8
  N2: PIR1.SIG, U1.Pin_2
  N3: PIR1.GND, U1.Pin_4, LED1.cathode, J1.pin1, U2.NC
  N4: U1.Pin_3, U2.COIL1
  N5: U1.Pin_6, U1.Pin_7, R1.Pin_0, R2.Pin_0
  N6: LED1.anode, R1.Pin_1
  N7: J1.pin2, R2.Pin_1
